// Logisim project ALU.circ as structural Verilog: 12 circuits, main circuit main
module main (
);

  ALU alu_1 ();  // open: A, B, Codop, CarryIn, Shift, S, Flags
endmodule

module BIT_POIDS_FORT (
  input  [31:0] in_1,
  output out_2
);

  // Probe on in_1[31]

  assign out_2 = in_1[31];
endmodule

module overadd (
  input  a,
  input  b,
  input  c,
  output s
);

  wire and_1_out, and_2_out, not_1_out, not_2_out, not_3_out;

  not not_1 (not_1_out, a);
  not not_2 (not_2_out, b);
  not not_3 (not_3_out, c);
  and and_1 (and_1_out, not_1_out, not_2_out, c);
  and and_2 (and_2_out, a, b, not_3_out);
  or or_1 (s, and_1_out, and_2_out);
endmodule

module overcmp (
  input  A,
  input  B,
  input  R,
  output V
);

  wire and_1_out, and_2_out, not_1_out, not_2_out, not_3_out;

  not not_1 (not_1_out, A);
  not not_2 (not_2_out, B);
  not not_3 (not_3_out, R);
  and and_1 (and_1_out, not_1_out, B, R);
  and and_2 (and_2_out, A, not_2_out, not_3_out);
  or or_1 (V, and_1_out, and_2_out);
endmodule

module multiplieur (
  input  [31:0] a,
  input  [31:0] b,
  output [31:0] res,
  output [31:0] Cout
);

  wire adder_1_cout, adder_2_cout, adder_3_cout, adder_4_cout, adder_5_cout, adder_6_cout, adder_7_cout,
       adder_8_cout;
  wire [15:0] multiplier_1_cout, multiplier_1_out, multiplier_2_cout, multiplier_2_out, multiplier_3_cout,
       multiplier_3_out, multiplier_4_cout, multiplier_4_out;
  wire [31:0] adder_1_out, adder_2_out, adder_4_out, adder_5_out, adder_6_out, adder_7_out, and_1_out,
       and_2_out, and_3_out, and_4_out, and_5_out, and_6_out, bit_extender_1_out, bit_extender_2_out,
       bit_extender_3_out, bit_extender_4_out, bit_extender_5_out, bit_extender_6_out, bit_extender_7_out,
       bit_extender_8_out, bit_extender_9_out, bit_extender_10_out, bit_extender_11_out, or_1_out,
       shifter_1_out, shifter_2_out, shifter_3_out, shifter_4_out, shifter_5_out, shifter_6_out;

  // Probe on multiplier_1_cout
  // Probe on multiplier_2_cout
  // Probe on a[31:16]
  // Probe on multiplier_3_cout
  // Probe on b[31:16]
  // Probe on multiplier_1_out
  Multiplier #(.width(16)) multiplier_1 (
    .a(a[31:16]), .b(b[15:0]), .out(multiplier_1_out), .cin({16{1'b0}}), .cout(multiplier_1_cout));
  assign bit_extender_1_out = {{16{multiplier_1_cout[15]}}, multiplier_1_cout};  // Bit_Extender bit_extender_1
  Multiplier #(.width(16)) multiplier_2 (
    .a(a[15:0]), .b(b[31:16]), .out(multiplier_2_out), .cin({16{1'b0}}), .cout(multiplier_2_cout));
  // Probe on multiplier_3_out
  Multiplier #(.width(16)) multiplier_3 (
    .a(a[31:16]), .b(b[31:16]), .out(multiplier_3_out), .cin({16{1'b0}}), .cout(multiplier_3_cout));
  // Probe on bit_extender_2_out
  assign bit_extender_2_out = {{16{multiplier_3_cout[15]}}, multiplier_3_cout};  // Bit_Extender bit_extender_2
  // Probe on shifter_1_out
  assign bit_extender_3_out = {{16{multiplier_1_out[15]}}, multiplier_1_out};  // Bit_Extender bit_extender_3
  assign and_1_out = bit_extender_1_out & 32'hffff;  // AND_Gate and_1, 32 bits wide
  assign bit_extender_4_out = {{16{multiplier_2_out[15]}}, multiplier_2_out};  // Bit_Extender bit_extender_4
  assign bit_extender_5_out = {{16{multiplier_2_cout[15]}}, multiplier_2_cout};  // Bit_Extender bit_extender_5
  // Probe on bit_extender_6_out
  assign bit_extender_6_out = {{16{multiplier_3_out[15]}}, multiplier_3_out};  // Bit_Extender bit_extender_6
  Shifter #(.width(32)) shifter_1 (.in(bit_extender_2_out), .\dist (5'b10000), .out(shifter_1_out));
  Multiplier #(.width(16)) multiplier_4 (
    .a(a[15:0]), .b(b[15:0]), .out(multiplier_4_out), .cin({16{1'b0}}), .cout(multiplier_4_cout));
  assign bit_extender_7_out = {{16{multiplier_4_cout[15]}}, multiplier_4_cout};  // Bit_Extender bit_extender_7
  // Probe on bit_extender_7_out
  // Probe on shifter_2_out
  Shifter #(.width(32)) shifter_2 (.in(bit_extender_3_out), .\dist (5'b10000), .out(shifter_2_out));
  // Probe on and_1_out
  // Probe on shifter_3_out
  Shifter #(.width(32)) shifter_3 (.in(bit_extender_4_out), .\dist (5'b10000), .out(shifter_3_out));
  // Probe on bit_extender_5_out
  Shifter #(.width(32)) shifter_4 (.in(bit_extender_6_out), .\dist (5'b10000), .out(shifter_4_out));
  assign and_2_out = 32'hffff & bit_extender_6_out;  // AND_Gate and_2, 32 bits wide
  assign or_1_out = shifter_1_out | and_2_out;  // OR_Gate or_1, 32 bits wide
  // Probe on multiplier_4_out
  // Probe on multiplier_4_cout
  Shifter #(.width(32)) shifter_5 (.in(bit_extender_7_out), .\dist (5'b10000), .out(shifter_5_out));
  // Probe on shifter_6_out
  Shifter #(.width(32)) shifter_6 (.in(shifter_4_out), .\dist (5'b10000), .out(shifter_6_out));
  // Probe on bit_extender_6_out
  // Probe on and_2_out
  assign bit_extender_8_out = {{16{multiplier_4_out[15]}}, multiplier_4_out};  // Bit_Extender bit_extender_8
  // Probe on or_1_out
  assign and_3_out = 32'hffff & bit_extender_8_out;  // AND_Gate and_3, 32 bits wide
  // Probe on and_3_out
  Adder #(.width(32)) adder_1 (.a(and_3_out), .b(shifter_2_out), .out(adder_1_out), .cin(1'b0), .cout(adder_1_cout));
  // Probe on adder_1_cout
  Adder #(.width(32)) adder_2 (
    .a(shifter_5_out), .b(adder_1_out), .out(adder_2_out), .cout(adder_2_cout));  // open: cin
  // Probe on adder_2_cout
  Adder #(.width(32)) adder_3 (.a(adder_2_out), .b(shifter_3_out), .out(res), .cout(adder_3_cout));  // open: cin
  assign bit_extender_9_out = {{31{adder_1_cout}}, adder_1_cout};  // Bit_Extender bit_extender_9
  assign bit_extender_10_out = {{31{adder_2_cout}}, adder_2_cout};  // Bit_Extender bit_extender_10
  assign bit_extender_11_out = {{31{adder_3_cout}}, adder_3_cout};  // Bit_Extender bit_extender_11
  assign and_4_out = 32'h1 & bit_extender_9_out;  // AND_Gate and_4, 32 bits wide
  // Probe on and_5_out
  assign and_5_out = 32'h1 & bit_extender_10_out;  // AND_Gate and_5, 32 bits wide
  assign and_6_out = bit_extender_11_out & 32'h1;  // AND_Gate and_6, 32 bits wide
  // Probe on and_4_out
  // Probe on adder_4_cout
  // Probe on adder_5_cout
  Adder #(.width(32)) adder_4 (.a(and_4_out), .b(and_5_out), .out(adder_4_out), .cin(1'b0), .cout(adder_4_cout));
  // Probe on adder_4_out
  Adder #(.width(32)) adder_5 (.a(adder_4_out), .b(and_6_out), .out(adder_5_out), .cout(adder_5_cout));  // open: cin
  // Probe on adder_5_out
  Adder #(.width(32)) adder_6 (.a(adder_5_out), .b(and_1_out), .out(adder_6_out), .cout(adder_6_cout));  // open: cin
  // Probe on adder_6_cout
  // Probe on adder_6_out
  // Probe on adder_7_out
  Adder #(.width(32)) adder_7 (
    .a(adder_6_out), .b(bit_extender_5_out), .out(adder_7_out), .cout(adder_7_cout));  // open: cin
  // Probe on adder_7_cout
  Adder #(.width(32)) adder_8 (.a(adder_7_out), .b(or_1_out), .out(Cout), .cout(adder_8_cout));  // open: cin
  // Probe on adder_8_cout

  // Other names for the same wires on the sheet: Af_t[15:0] = a[15:0]; AF[15:0] = a[31:16]; Bf_t[15:0] = b[15:0];
  //   BF[15:0] = b[31:16]
endmodule

module neg (
  input  [31:0] a,
  output isNeg
);

  // Probe on a[31]

  assign isNeg = a[31];
endmodule

module zero (
  input  [31:0] a,
  output isZero
);

  wire or_1_out;

  or or_1 (or_1_out, a[31], a[30], a[29], a[28], a[27], a[26], a[25], a[24], a[23], a[22], a[21], a[20], a[19], a[18], a[17], a[16], a[15], a[14], a[13], a[12], a[11], a[10], a[9], a[8], a[7], a[6], a[5], a[4], a[3], a[2], a[1], a[0]);
  not not_1 (isZero, or_1_out);
endmodule

module ALU (
  input  [31:0] A,
  input  [31:0] B,
  input  [3:0] Codop,
  input  CarryIn,
  input  [4:0] Shift,
  output [31:0] S,
  output [3:0] Flags
);

  wire adder_1_cout, adder_2_cout, BA, BB, bit_poids_fort_3_out_2, bit_poids_fort_4_out_2,
       bit_poids_fort_5_out_2, bitselector_2_out, carryasr, carrylsl, comparator_1_eq, overadd_1_s,
       overadd_2_s, overcmp_1_v, subtractor_2_bout, subtractor_3_bout, TST_CMP_CMN;
  wire [4:0] bit_extender_2_out, subtractor_1_out;
  wire [5:0] bit_extender_1_out, subtractor_5_out;
  wire [31:0] and_1_out, ASR, BIC, LSL, LSR, MUL, multiplexer_2_out, multiplieur_1_cout, negB, ORR, resADC,
       resCMN, resCMP, rot, RSB, SBC, subtractor_3_out, TST, xor_1_out;

  // Probe on A
  assign bit_extender_1_out = {{1{1'b0}}, Shift};  // Bit_Extender bit_extender_1
  Subtractor #(.width(5)) subtractor_1 (.a(Shift), .b(5'b00001), .out(subtractor_1_out));  // open: bin, bout
  assign negB = ~B;  // NOT_Gate not_1, 32 bits wide
  BitSelector #(.width(32)) bitselector_1 (.in(B), .out(carryasr), .sel(subtractor_1_out));
  multiplieur multiplieur_1 (.a(A), .b(B), .res(MUL), .Cout(multiplieur_1_cout));
  // Probe on multiplieur_1_cout
  Adder #(.width(32)) adder_1 (.a(A), .b(B), .out(resCMN), .cout(adder_1_cout));  // open: cin
  Subtractor #(.width(32)) subtractor_2 (.a(B), .b(A), .out(resCMP), .bout(subtractor_2_bout));  // open: bin
  Adder #(.width(32)) adder_2 (.a(A), .b(B), .out(resADC), .cin(CarryIn), .cout(adder_2_cout));
  Subtractor #(.width(32)) subtractor_3 (.a(B), .b(A), .out(subtractor_3_out), .bin(CarryIn), .bout(subtractor_3_bout));
  Shifter #(.width(32)) shifter_1 (.in(B), .\dist (Shift), .out(LSL));
  Shifter #(.width(32), .shift("lr")) shifter_2 (.in(B), .\dist (Shift), .out(LSR));
  Shifter #(.width(32), .shift("ar")) shifter_3 (.in(B), .\dist (Shift), .out(ASR));
  Shifter #(.width(32), .shift("rr")) shifter_4 (.in(B), .\dist (Shift), .out(rot));
  Subtractor #(.width(32)) subtractor_4 (.a({32{1'b0}}), .b(A), .out(RSB));  // open: bin, bout
  Subtractor #(.width(6)) subtractor_5 (
    .a(6'b100000), .b(bit_extender_1_out), .out(subtractor_5_out));  // open: bin, bout
  // Probe on subtractor_5_out
  // Probe on MUL
  assign and_1_out = A & B;  // AND_Gate and_1, 32 bits wide
  assign xor_1_out = A ^ B;  // XOR_Gate xor_1, 32 bits wide
  assign BIC = A & negB;  // AND_Gate and_2, 32 bits wide
  assign ORR = A | B;  // OR_Gate or_1, 32 bits wide
  assign TST = A & B;  // AND_Gate and_3, 32 bits wide
  BitSelector #(.width(32)) bitselector_2 (.in(B), .out(bitselector_2_out), .sel(bit_extender_2_out));
  Bit_Extender #(.in_width(6), .out_width(5), .\type ("zero")) bit_extender_2 (
    .in(subtractor_5_out), .out(bit_extender_2_out));
  // Probe on bit_extender_2_out
  Adder #(.width(32)) adder_3 (.a(subtractor_3_out), .b(32'h1), .out(SBC));  // open: cin, cout
  Comparator #(.width(5), .mode("unsigned")) comparator_1 (
    .a(Shift), .b({5{1'b0}}), .eq(comparator_1_eq));  // open: gt, lt
  Subtractor #(.width(32)) subtractor_6 ();  // open: a, b, out, bin, bout
  // Probe on carrylsl
  Multiplexer #(.enable("false")) multiplexer_1 (
    .in0(bitselector_2_out), .in1(1'b0), .out(carrylsl), .sel(comparator_1_eq));
  isTST_CMP_CMN istst_cmp_cmn_1 (.a(Codop[3]), .b(Codop[2]), .c(Codop[1]), .d(Codop[0]), .s(TST_CMP_CMN));
  Multiplexer #(.select(4), .width(32), .enable("false")) multiplexer_2 (
    .in0(and_1_out), .in1(xor_1_out), .in2(LSL), .in3(LSR), .in4(ASR), .in5(resADC), .in6(SBC), .in7(rot),
    .in8(TST), .in9(RSB), .in10(resCMP), .in11(resCMN), .in12(ORR), .in13(MUL), .in14(BIC), .in15(negB),
    .out(multiplexer_2_out), .sel(Codop));
  // Probe on A
  // Probe on B
  Multiplexer #(.select(4), .enable("false")) multiplexer_3 (
    .in0(1'b0), .in1(1'b0), .in2(carrylsl), .in3(carryasr), .in4(carryasr), .in5(adder_2_cout),
    .in6(subtractor_3_bout), .in7(1'b0), .in8(1'b0), .in9(1'b0), .in10(subtractor_2_bout),
    .in11(adder_1_cout), .in12(1'b0), .in13(1'b0), .in14(1'b0), .in15(1'b0), .out(Flags[1]), .sel(Codop));
  // Probe on Flags[1]
  BIT_POIDS_FORT bit_poids_fort_1 (.in_1(A), .out_2(BA));
  BIT_POIDS_FORT bit_poids_fort_2 (.in_1(B), .out_2(BB));
  BIT_POIDS_FORT bit_poids_fort_3 (.in_1(resADC), .out_2(bit_poids_fort_3_out_2));
  BIT_POIDS_FORT bit_poids_fort_4 (.in_1(resCMP), .out_2(bit_poids_fort_4_out_2));
  BIT_POIDS_FORT bit_poids_fort_5 (.in_1(resCMN), .out_2(bit_poids_fort_5_out_2));
  Multiplexer #(.width(32), .enable("false")) multiplexer_4 (
    .in0(multiplexer_2_out), .in1(B), .out(S), .sel(TST_CMP_CMN));
  // Probe on resCMP
  overadd overadd_1 (.a(BA), .b(BB), .c(bit_poids_fort_3_out_2), .s(overadd_1_s));
  overcmp overcmp_1 (.A(BA), .B(BB), .R(bit_poids_fort_4_out_2), .V(overcmp_1_v));
  overadd overadd_2 (.a(BA), .b(BB), .c(bit_poids_fort_5_out_2), .s(overadd_2_s));
  zero zero_1 (.a(multiplexer_2_out), .isZero(Flags[2]));
  // Probe on Flags[2]
  // Probe on Flags[3]
  neg neg_1 (.a(multiplexer_2_out), .isNeg(Flags[3]));
  Multiplexer #(.select(4), .enable("false")) multiplexer_5 (
    .in0(1'b0), .in1(1'b0), .in2(1'b0), .in3(1'b0), .in4(1'b0), .in5(overadd_1_s), .in6(1'b0), .in7(1'b0),
    .in8(1'b0), .in9(1'b0), .in10(overcmp_1_v), .in11(overadd_2_s), .in12(1'b0), .in13(1'b0), .in14(1'b0),
    .in15(1'b0), .out(Flags[0]), .sel(Codop));

  // Other names for the same wires on the sheet: carrylsr = carryasr; sel[3:0] = Codop; tunShift[4:0] = Shift
endmodule

module brouillon_ALU (
  input  in_1,
  input  in_2
);

  wire adder_1_cout, adder_2_cout, BA, BB, bit_poids_fort_3_out_2, bit_poids_fort_4_out_2,
       bit_poids_fort_5_out_2, comparator_1_eq, multiplexer_2_out, neg_1_isneg, overadd_1_s, overadd_2_s,
       overcmp_1_v, subtractor_1_bout, subtractor_2_bout;
  wire [31:0] and_1_out, ASR, BIC, LSL, LSR, MUL, multiplexer_1_out, negB, ORR, resADC, resCMN, resCMP, rot,
       RSB, SBC, subtractor_2_out, TST, xor_1_out;

  // Probe on 32'h2
  multiplieur multiplieur_1 (.a(32'h2), .b(32'hffff), .res(MUL));  // open: Cout
  assign negB = ~32'hffff;  // NOT_Gate not_1, 32 bits wide
  // Probe on MUL
  assign and_1_out = 32'h2 & 32'hffff;  // AND_Gate and_1, 32 bits wide
  assign xor_1_out = 32'h2 ^ 32'hffff;  // XOR_Gate xor_1, 32 bits wide
  assign BIC = 32'h2 & negB;  // AND_Gate and_2, 32 bits wide
  assign ORR = 32'h2 | 32'hffff;  // OR_Gate or_1, 32 bits wide
  Adder #(.width(32)) adder_1 (.a(32'h2), .b(32'hffff), .out(resCMN), .cout(adder_1_cout));  // open: cin
  Subtractor #(.width(32)) subtractor_1 (.a(32'h2), .b(32'hffff), .out(resCMP), .bout(subtractor_1_bout));  // open: bin
  Adder #(.width(32)) adder_2 (.a(32'h2), .b(32'hffff), .out(resADC), .cin(in_1), .cout(adder_2_cout));
  Subtractor #(.width(32)) subtractor_2 (
    .a(32'h2), .b(32'hffff), .out(subtractor_2_out), .bin(in_1), .bout(subtractor_2_bout));
  Shifter #(.width(32)) shifter_1 (.in(32'hffff), .\dist (5'b00001), .out(LSL));
  Shifter #(.width(32), .shift("lr")) shifter_2 (.in(32'hffff), .\dist (5'b00001), .out(LSR));
  Shifter #(.width(32), .shift("ar")) shifter_3 (.in(32'hffff), .\dist (5'b00001), .out(ASR));
  Shifter #(.width(32), .shift("rr")) shifter_4 (.in(32'hffff), .\dist (5'b00001), .out(rot));
  Subtractor #(.width(32)) subtractor_3 (.a({32{1'b0}}), .b(32'h2), .out(RSB));  // open: bin, bout
  assign TST = 32'h2 & 32'hffff;  // AND_Gate and_3, 32 bits wide
  Subtractor #(.width(32)) subtractor_4 (.a(subtractor_2_out), .b(32'h1), .out(SBC));  // open: bin, bout
  Multiplexer #(.select(4), .width(32), .enable("false")) multiplexer_1 (
    .in0(and_1_out), .in1(xor_1_out), .in2(LSL), .in3(LSR), .in4(ASR), .in5(resADC), .in6(SBC), .in7(rot),
    .in8(TST), .in9(RSB), .in10(resCMP), .in11(resCMN), .in12(ORR), .in13(MUL), .in14(BIC), .in15(negB),
    .out(multiplexer_1_out), .sel(4'b1001));
  // Probe on 32'hffff
  // Probe on 32'h2
  // Probe on multiplexer_2_out
  Multiplexer #(.select(4), .enable("false")) multiplexer_2 (
    .in0(1'b0), .in1(1'b0), .in2(1'b0), .in3(1'b0), .in4(1'b0), .in5(adder_2_cout), .in6(subtractor_2_bout),
    .in7(1'b0), .in8(1'b0), .in9(1'b0), .in10(subtractor_1_bout), .in11(adder_1_cout), .in12(1'b0),
    .in13(1'b0), .in14(1'b0), .in15(1'b0), .out(multiplexer_2_out), .sel(4'b1001));
  BIT_POIDS_FORT bit_poids_fort_1 (.in_1(32'h2), .out_2(BA));
  BIT_POIDS_FORT bit_poids_fort_2 (.in_1(32'hffff), .out_2(BB));
  BIT_POIDS_FORT bit_poids_fort_3 (.in_1(resADC), .out_2(bit_poids_fort_3_out_2));
  BIT_POIDS_FORT bit_poids_fort_4 (.in_1(resCMP), .out_2(bit_poids_fort_4_out_2));
  BIT_POIDS_FORT bit_poids_fort_5 (.in_1(resCMN), .out_2(bit_poids_fort_5_out_2));
  Comparator #(.width(32)) comparator_1 (.a(multiplexer_1_out), .b({32{1'b0}}), .eq(comparator_1_eq));  // open: gt, lt
  // Probe on multiplexer_1_out
  // Probe on comparator_1_eq
  // Probe on neg_1_isneg
  neg neg_1 (.a(multiplexer_1_out), .isNeg(neg_1_isneg));
  overadd overadd_1 (.a(BA), .b(BB), .c(bit_poids_fort_3_out_2), .s(overadd_1_s));
  overcmp overcmp_1 (.A(BA), .B(BB), .R(bit_poids_fort_4_out_2), .V(overcmp_1_v));
  overadd overadd_2 (.a(BA), .b(BB), .c(bit_poids_fort_5_out_2), .s(overadd_2_s));
  Multiplexer #(.select(4), .enable("false")) multiplexer_3 (
    .in5(overadd_1_s), .in9(1'b0), .in10(overcmp_1_v), .in11(overadd_2_s), .out(in_2), .sel(4'b1001));  // open: in0, in1, in2, in3, in4, in6, in7, in8, in12, in13, in14, in15
endmodule

module brouillon_MUL (
);

  wire adder_1_cout, adder_2_cout, adder_3_cout, adder_4_cout, adder_5_cout, adder_6_cout, adder_7_cout,
       adder_8_cout;
  wire [15:0] multiplier_1_cout, multiplier_1_out, multiplier_2_cout, multiplier_2_out, multiplier_3_cout,
       multiplier_3_out, multiplier_4_cout, multiplier_4_out;
  wire [31:0] adder_1_out, adder_2_out, adder_3_out, adder_4_out, adder_5_out, adder_6_out, adder_7_out,
       adder_8_out, and_1_out, and_2_out, and_3_out, and_4_out, and_5_out, and_6_out, bit_extender_1_out,
       bit_extender_2_out, bit_extender_3_out, bit_extender_4_out, bit_extender_5_out, bit_extender_6_out,
       bit_extender_7_out, bit_extender_8_out, bit_extender_9_out, bit_extender_10_out, bit_extender_11_out,
       or_1_out, shifter_1_out, shifter_2_out, shifter_3_out, shifter_4_out, shifter_5_out, shifter_6_out;

  // Probe on multiplier_1_cout
  // Probe on multiplier_2_cout
  // Probe on 16'hf0f
  // Probe on multiplier_3_cout
  // Probe on 16'hf0f
  // Probe on multiplier_1_out
  Multiplier #(.width(16)) multiplier_1 (
    .a(16'hf0f), .b(16'habde), .out(multiplier_1_out), .cin({16{1'b0}}), .cout(multiplier_1_cout));
  assign bit_extender_1_out = {{16{multiplier_1_cout[15]}}, multiplier_1_cout};  // Bit_Extender bit_extender_1
  Multiplier #(.width(16)) multiplier_2 (
    .a(16'habde), .b(16'hf0f), .out(multiplier_2_out), .cin({16{1'b0}}), .cout(multiplier_2_cout));
  // Probe on multiplier_3_out
  Multiplier #(.width(16)) multiplier_3 (
    .a(16'hf0f), .b(16'hf0f), .out(multiplier_3_out), .cin({16{1'b0}}), .cout(multiplier_3_cout));
  // Probe on bit_extender_2_out
  assign bit_extender_2_out = {{16{multiplier_3_cout[15]}}, multiplier_3_cout};  // Bit_Extender bit_extender_2
  // Probe on shifter_1_out
  assign bit_extender_3_out = {{16{multiplier_1_out[15]}}, multiplier_1_out};  // Bit_Extender bit_extender_3
  assign and_1_out = bit_extender_1_out & 32'hffff;  // AND_Gate and_1, 32 bits wide
  assign bit_extender_4_out = {{16{multiplier_2_out[15]}}, multiplier_2_out};  // Bit_Extender bit_extender_4
  assign bit_extender_5_out = {{16{multiplier_2_cout[15]}}, multiplier_2_cout};  // Bit_Extender bit_extender_5
  // Probe on bit_extender_6_out
  assign bit_extender_6_out = {{16{multiplier_3_out[15]}}, multiplier_3_out};  // Bit_Extender bit_extender_6
  Shifter #(.width(32)) shifter_1 (.in(bit_extender_2_out), .\dist (5'b10000), .out(shifter_1_out));
  Multiplier #(.width(16)) multiplier_4 (
    .a(16'habde), .b(16'habde), .out(multiplier_4_out), .cin({16{1'b0}}), .cout(multiplier_4_cout));
  assign bit_extender_7_out = {{16{multiplier_4_cout[15]}}, multiplier_4_cout};  // Bit_Extender bit_extender_7
  // Probe on bit_extender_7_out
  // Probe on shifter_2_out
  Shifter #(.width(32)) shifter_2 (.in(bit_extender_3_out), .\dist (5'b10000), .out(shifter_2_out));
  // Probe on and_1_out
  // Probe on shifter_3_out
  Shifter #(.width(32)) shifter_3 (.in(bit_extender_4_out), .\dist (5'b10000), .out(shifter_3_out));
  // Probe on bit_extender_5_out
  Shifter #(.width(32)) shifter_4 (.in(bit_extender_6_out), .\dist (5'b10000), .out(shifter_4_out));
  assign and_2_out = 32'hffff & bit_extender_6_out;  // AND_Gate and_2, 32 bits wide
  assign or_1_out = shifter_1_out | and_2_out;  // OR_Gate or_1, 32 bits wide
  // Probe on multiplier_4_out
  // Probe on multiplier_4_cout
  Shifter #(.width(32)) shifter_5 (.in(bit_extender_7_out), .\dist (5'b10000), .out(shifter_5_out));
  // Probe on shifter_6_out
  Shifter #(.width(32)) shifter_6 (.in(shifter_4_out), .\dist (5'b10000), .out(shifter_6_out));
  // Probe on bit_extender_6_out
  // Probe on and_2_out
  assign bit_extender_8_out = {{16{multiplier_4_out[15]}}, multiplier_4_out};  // Bit_Extender bit_extender_8
  // Probe on or_1_out
  assign and_3_out = 32'hffff & bit_extender_8_out;  // AND_Gate and_3, 32 bits wide
  // Probe on and_3_out
  Adder #(.width(32)) adder_1 (.a(and_3_out), .b(shifter_2_out), .out(adder_1_out), .cin(1'b0), .cout(adder_1_cout));
  // Probe on adder_1_cout
  Adder #(.width(32)) adder_2 (
    .a(shifter_5_out), .b(adder_1_out), .out(adder_2_out), .cout(adder_2_cout));  // open: cin
  // Probe on adder_2_cout
  Adder #(.width(32)) adder_3 (
    .a(adder_2_out), .b(shifter_3_out), .out(adder_3_out), .cout(adder_3_cout));  // open: cin
  assign bit_extender_9_out = {{31{adder_1_cout}}, adder_1_cout};  // Bit_Extender bit_extender_9
  assign bit_extender_10_out = {{31{adder_2_cout}}, adder_2_cout};  // Bit_Extender bit_extender_10
  assign bit_extender_11_out = {{31{adder_3_cout}}, adder_3_cout};  // Bit_Extender bit_extender_11
  assign and_4_out = 32'h1 & bit_extender_9_out;  // AND_Gate and_4, 32 bits wide
  // Probe on and_5_out
  assign and_5_out = 32'h1 & bit_extender_10_out;  // AND_Gate and_5, 32 bits wide
  // Probe on adder_3_out
  assign and_6_out = bit_extender_11_out & 32'h1;  // AND_Gate and_6, 32 bits wide
  // Probe on and_4_out
  // Probe on adder_4_cout
  // Probe on adder_5_cout
  Adder #(.width(32)) adder_4 (.a(and_4_out), .b(and_5_out), .out(adder_4_out), .cin(1'b0), .cout(adder_4_cout));
  // Probe on adder_4_out
  Adder #(.width(32)) adder_5 (.a(adder_4_out), .b(and_6_out), .out(adder_5_out), .cout(adder_5_cout));  // open: cin
  // Probe on adder_5_out
  Adder #(.width(32)) adder_6 (.a(adder_5_out), .b(and_1_out), .out(adder_6_out), .cout(adder_6_cout));  // open: cin
  // Probe on adder_6_cout
  // Probe on adder_6_out
  // Probe on adder_7_out
  Adder #(.width(32)) adder_7 (
    .a(adder_6_out), .b(bit_extender_5_out), .out(adder_7_out), .cout(adder_7_cout));  // open: cin
  // Probe on adder_7_cout
  // Probe on adder_8_out
  Adder #(.width(32)) adder_8 (.a(adder_7_out), .b(or_1_out), .out(adder_8_out), .cout(adder_8_cout));  // open: cin
  // Probe on adder_8_cout
endmodule

module brouillon_banc_reg (
);

  wire clock_1_out;
  wire [31:0] register_1_q;

  D_Flip_Flop d_ff_1 ();  // open: clk, D, Q, Qn, preset, reset
  D_Flip_Flop d_ff_2 ();  // open: clk, D, Q, Qn, preset, reset
  Clock clock_1 (.out(clock_1_out));
  Demultiplexer #(.select(3), .width(32), .enable("false")) demultiplexer_1 (
    .in(32'habcd), .sel(3'b111));  // open: out0, out1, out2, out3, out4, out5, out6, out7
  Register #(.width(32)) register_1 (.D(32'habcffe), .en(1'b1), .clk(clock_1_out), .Q(register_1_q), .clr(1'b1));
  // Probe on register_1_q
endmodule

module isTST_CMP_CMN (
  input  a,
  input  b,
  input  c,
  input  d,
  output s
);

  wire and_1_out, and_2_out, and_3_out, not_1_out, not_2_out, not_3_out, not_4_out, not_5_out, not_6_out;

  not not_1 (not_1_out, b);
  not not_2 (not_2_out, c);
  not not_3 (not_3_out, d);
  not not_4 (not_4_out, b);
  not not_5 (not_5_out, d);
  not not_6 (not_6_out, b);
  and and_1 (and_1_out, a, not_1_out, not_2_out, not_3_out);
  or or_1 (s, and_1_out, and_2_out, and_3_out);
  and and_2 (and_2_out, a, not_4_out, c, not_5_out);
  and and_3 (and_3_out, a, not_6_out, c, d);
endmodule
