// Logisim project BancDeRegistres.circ as structural Verilog: 3 circuits, main circuit BANC_REGISTRE
module BANC_REGISTRE (
  input  [31:0] DataIn,
  input  Clk,
  input  [2:0] RegA,
  input  [2:0] RegB,
  input  [2:0] RegDest,
  input  Reset,
  output [31:0] AOut,
  output [31:0] AffR0,
  output [31:0] AffR1,
  output [31:0] AffR2,
  output [31:0] AffR3,
  output [31:0] AffR4,
  output [31:0] AffR5,
  output [31:0] BOut,
  output [31:0] AffR6,
  output [31:0] AffrR7
);

  wire decoder_1_out0, decoder_1_out1, decoder_1_out2, decoder_1_out3, decoder_1_out4, decoder_1_out5,
       decoder_1_out6, decoder_1_out7;

  Decoder #(.select(3)) decoder_1 (
    .out0(decoder_1_out0), .out1(decoder_1_out1), .out2(decoder_1_out2), .out3(decoder_1_out3),
    .out4(decoder_1_out4), .out5(decoder_1_out5), .out6(decoder_1_out6), .out7(decoder_1_out7), .sel(RegDest));  // open: en
  Register #(.width(32)) R0 (.D(DataIn), .en(decoder_1_out0), .clk(Clk), .Q(AffR0), .clr(Reset));
  Register #(.width(32)) R1 (.D(DataIn), .en(decoder_1_out1), .clk(Clk), .Q(AffR1), .clr(Reset));
  Register #(.width(32)) R2 (.D(DataIn), .en(decoder_1_out2), .clk(Clk), .Q(AffR2), .clr(Reset));
  Register #(.width(32)) R3 (.D(DataIn), .en(decoder_1_out3), .clk(Clk), .Q(AffR3), .clr(Reset));
  Register #(.width(32)) R4 (.D(DataIn), .en(decoder_1_out4), .clk(Clk), .Q(AffR4), .clr(Reset));
  Register #(.width(32)) R5 (.D(DataIn), .en(decoder_1_out5), .clk(Clk), .Q(AffR5), .clr(Reset));
  Register #(.width(32)) R6 (.D(DataIn), .en(decoder_1_out6), .clk(Clk), .Q(AffR6), .clr(Reset));
  Register #(.width(32)) R7 (.D(DataIn), .en(decoder_1_out7), .clk(Clk), .Q(AffrR7), .clr(Reset));
  Multiplexer #(.select(3), .width(32), .enable("false")) multiplexer_1 (
    .in0(AffR0), .in1(AffR1), .in2(AffR2), .in3(AffR3), .in4(AffR4), .in5(AffR5), .in6(AffR6), .in7(AffrR7),
    .out(AOut), .sel(RegA));
  Multiplexer #(.select(3), .width(32), .enable("false")) multiplexer_2 (
    .in0(AffR0), .in1(AffR1), .in2(AffR2), .in3(AffR3), .in4(AffR4), .in5(AffR5), .in6(AffR6), .in7(AffrR7),
    .out(BOut), .sel(RegB));
endmodule

module Test_Banc_Registre (
);

  wire clock_1_out, undriven, undriven_2;

  Clock clock_1 (.out(clock_1_out));
  BANC_REGISTRE banc_registre_1 ();  // open: AffR4, AffR3, AffR2, AffR1, AffR0, AOut, Reset, RegDest, RegB, RegA, Clk, DataIn, AffR5, BOut, AffR6, AffrR7
  // Probe on nothing
  // Probe on nothing
  // Probe on nothing
  // Probe on nothing
  // Probe on nothing
  // Probe on nothing
  // Probe on nothing
  // Probe on nothing
  // Probe on undriven
  // Probe on undriven_2
endmodule

module BancRegistre (
  input  [31:0] DataIn,
  input  [2:0] RegDest,
  input  Clk,
  input  Reset,
  input  [2:0] RegA,
  input  [2:0] RegB,
  output [31:0] AOut,
  output [31:0] BOut,
  output [31:0] R0,
  output [31:0] R1,
  output [31:0] R2,
  output [31:0] R3,
  output [31:0] R4,
  output [31:0] R5,
  output [31:0] R6,
  output [31:0] R7
);

  BANC_REGISTRE banc_registre_1 (
    .AffR4(R4), .AffR3(R3), .AffR2(R2), .AffR1(R1), .AffR0(R0), .AOut(AOut), .Reset(Reset),
    .RegDest(RegDest), .RegB(RegB), .RegA(RegA), .Clk(Clk), .DataIn(DataIn), .AffR5(R5), .BOut(BOut),
    .AffR6(R6), .AffrR7(R7));
endmodule
