// Logisim project Controller.circ as structural Verilog
module Controller (
  input  [15:0] Inst,
  input  [3:0] Flags,
  input  Clk,
  input  Reset,
  output Carry,
  output DP_Shift,
  output Imm32_Enable,
  output [4:0] Imm5,
  output [31:0] Imm32,
  output [3:0] ALU_Opcode,
  output [2:0] Rm,
  output [2:0] Rn,
  output [2:0] Rd,
  output [31:0] RAM_Addr,
  output Load,
  output Store,
  output [7:0] PC
);

  wire Conditional_1_verified, load_store_1_pc_hold, not_1_out, opcode_decoder_1_conditional,
       opcode_decoder_1_data_processing, opcode_decoder_1_load_store, opcode_decoder_1_shift,
       opcode_decoder_1_sp_address, shift_add_sub_mov_1_carry, sp_address_1_write_enable;
  wire [2:0] data_processing_1_rd, data_processing_1_rm, data_processing_1_rn, load_store_1_rd,
       load_store_1_rm, shift_add_sub_mov_1_rd, shift_add_sub_mov_1_rm, shift_add_sub_mov_1_rn;
  wire [3:0] data_processing_1_alu_opcode, data_processing_1_flags_update_mask, flags_apsr_1_flags_out,
       or_1_out, shift_add_sub_mov_1_alu_opcode, shift_add_sub_mov_1_flags_update_mask;
  wire [7:0] adder_1_out, adder_2_out, Conditional_1_offset;
  wire [31:0] sp_address_1_new_stack_pointer, Stack_Pointer_q;

  Register #(.width(32)) Stack_Pointer (
    .D(sp_address_1_new_stack_pointer), .en(sp_address_1_write_enable), .clk(Clk), .Q(Stack_Pointer_q),
    .clr(Reset));
  // Probe on Inst
  // Probe on Stack_Pointer_q
  Opcode_Decoder opcode_decoder_1 (
    .Opcode(Inst[15:10]), .Shift(opcode_decoder_1_shift), .Data_Processing(opcode_decoder_1_data_processing),
    .Load_Store(opcode_decoder_1_load_store), .SP_Address(opcode_decoder_1_sp_address),
    .Conditional(opcode_decoder_1_conditional));
  assign or_1_out = data_processing_1_flags_update_mask | shift_add_sub_mov_1_flags_update_mask;  // OR_Gate or_1, 4 bits wide
  Shift_Add_Sub_Mov shift_add_sub_mov_1 (
    .Imm32_Enable(Imm32_Enable), .ALU_Opcode(shift_add_sub_mov_1_alu_opcode), .Instruction(Inst),
    .Enable(opcode_decoder_1_shift), .Carry(shift_add_sub_mov_1_carry),
    .Flags_Update_Mask(shift_add_sub_mov_1_flags_update_mask), .Rd(shift_add_sub_mov_1_rd),
    .Rn(shift_add_sub_mov_1_rn), .Rm(shift_add_sub_mov_1_rm), .Imm5(Imm5), .Imm32(Imm32));
  // Probe on data_processing_1_rm
  Data_Processing data_processing_1 (
    .Instruction(Inst), .Enable(opcode_decoder_1_data_processing), .Rn(data_processing_1_rn),
    .Rd(data_processing_1_rd), .Rm(data_processing_1_rm), .ALU_Opcode(data_processing_1_alu_opcode),
    .Flags_Update_Mask(data_processing_1_flags_update_mask));
  Flags_APSR flags_apsr_1 (
    .Flags_In(Flags), .Update_Mask(or_1_out), .Clk(Clk), .Reset(Reset), .Flags_Out(flags_apsr_1_flags_out));
  Load_Store load_store_1 (
    .Rm(load_store_1_rm), .Instruction(Inst), .Rd(load_store_1_rd), .Load(Load),
    .Enable(opcode_decoder_1_load_store), .RAM_Addr(RAM_Addr), .Stack_Pointer(Stack_Pointer_q),
    .Store(Store), .PC_Hold(load_store_1_pc_hold), .Reset(Reset), .Clk(Clk));  // open: init2
  Conditional Conditional_1 (
    .Offset(Conditional_1_offset), .Instruction(Inst), .Enable(opcode_decoder_1_conditional),
    .Verified(Conditional_1_verified), .Z(flags_apsr_1_flags_out[2]), .V(flags_apsr_1_flags_out[0]),
    .N(flags_apsr_1_flags_out[3]), .C(flags_apsr_1_flags_out[1]));
  // Probe on shift_add_sub_mov_1_rd
  // Probe on data_processing_1_rn
  // Probe on data_processing_1_rd
  // Probe on flags_apsr_1_flags_out
  SP_Address sp_address_1 (
    .Stack_Pointer(Stack_Pointer_q), .Enable(opcode_decoder_1_sp_address),
    .Write_Enable(sp_address_1_write_enable), .Instruction(Inst),
    .New_Stack_Pointer(sp_address_1_new_stack_pointer));
  Adder adder_1 (.a(8'h3), .b(Conditional_1_offset), .out(adder_1_out), .cin(1'b0));  // open: cout
  // Probe on data_processing_1_alu_opcode
  Adder adder_2 (.a(adder_1_out), .b(PC), .out(adder_2_out), .cin(1'b0));  // open: cout
  and and_1 (DP_Shift, opcode_decoder_1_shift, ~opcode_decoder_1_data_processing);  // AND_Gate
  // Probe on shift_add_sub_mov_1_alu_opcode
  not not_1 (not_1_out, load_store_1_pc_hold);
  Counter counter_1 (
    .clr(Reset), .load(Conditional_1_verified), .up(1'b1), .count(not_1_out), .clk(Clk),
    .D(Conditional_1_offset), .Q(PC));  // open: carry
  Multiplexer #(.enable("false")) multiplexer_1 (
    .in0(flags_apsr_1_flags_out[1]), .in1(shift_add_sub_mov_1_carry), .out(Carry), .sel(DP_Shift));
  // Probe on load_store_1_rd
  assign ALU_Opcode = shift_add_sub_mov_1_alu_opcode | data_processing_1_alu_opcode;  // OR_Gate or_2, 4 bits wide
  assign Rm = shift_add_sub_mov_1_rm | data_processing_1_rm | load_store_1_rm;  // OR_Gate or_3, 3 bits wide
  assign Rn = shift_add_sub_mov_1_rn | load_store_1_rd | data_processing_1_rn;  // OR_Gate or_4, 3 bits wide
  assign Rd = shift_add_sub_mov_1_rd | data_processing_1_rd | load_store_1_rd;  // OR_Gate or_5, 3 bits wide

  // Notes on the sheet:
  //   Extract carry
  //   Extract Opcode
  //   IF Reg_Imm=1 THEN use shift value from register ELSE use shift value from Imm5
  //   Buffer flags for next instruction
  //   Add 3 to offset because ARM pre-increments PC
  //   and does an additionnal prefect operation
endmodule

module Conditional (
  input  Enable,
  input  [15:0] Instruction,
  input  N,
  input  Z,
  input  C,
  input  V,
  output [7:0] Offset,
  output Verified
);

  wire and_1_out, and_2_out, comparator_2_eq, eg, gt, le, multiplexer_1_out, not_1_out, not_2_out, not_3_out,
       not_4_out, not_5_out, not_6_out, not_7_out, not_8_out, not_9_out;

  not not_1 (not_1_out, Z);
  not not_2 (not_2_out, C);
  and and_1 (and_1_out, C, not_1_out);
  and and_2 (and_2_out, Z, not_2_out);
  not not_3 (not_3_out, Z);
  and and_3 (gt, not_3_out, eg);
  not not_4 (not_4_out, Z);
  not not_5 (not_5_out, C);
  not not_6 (not_6_out, N);
  not not_7 (not_7_out, V);
  not not_8 (not_8_out, eg);
  Comparator #(.width(1)) comparator_1 (.a(N), .b(V), .eq(eg));  // open: gt, lt
  Multiplexer #(.select(4), .enable("false")) multiplexer_1 (
    .in0(Z), .in1(not_4_out), .in2(C), .in3(not_5_out), .in4(N), .in5(not_6_out), .in6(V), .in7(not_7_out),
    .in8(and_1_out), .in9(and_2_out), .in10(eg), .in11(not_8_out), .in12(gt), .in13(le), .in14(1'b1),
    .out(multiplexer_1_out), .sel(Instruction[11:8]));  // open: in15
  Multiplexer #(.enable("false")) multiplexer_2 (.in0(1'b0), .in1(multiplexer_1_out), .out(Verified), .sel(Enable));
  Comparator #(.width(1)) comparator_2 (.a(N), .b(V), .eq(comparator_2_eq));  // open: gt, lt
  not not_9 (not_9_out, comparator_2_eq);
  or or_1 (le, Z, not_9_out);

  assign Offset = Instruction[7:0];

  // Other names for the same wires on the sheet: ena = Enable; imm8[7:0] = Instruction[7:0]; inst[15:0] = Instruction;
  //   opcode[3:0] = Instruction[11:8]
endmodule

module tenFirst (
  input  [15:0] in_1,
  output z
);

  wire and_1_out, not_1_out, not_2_out;

  not not_1 (not_1_out, in_1[6]);
  not not_2 (not_2_out, in_1[9]);
  and and_1 (and_1_out, in_1[8], not_1_out);
  or or_1 (z, not_2_out, and_1_out);
endmodule

module is14 (
  input  [15:0] in_1,
  output z
);

  and and_1 (z, in_1[9], in_1[8], in_1[7], in_1[6]);
endmodule

module is1516 (
  input  [15:0] in_1,
  output z
);

  wire not_1_out;

  not not_1 (not_1_out, in_1[7]);
  and and_1 (z, in_1[9], not_1_out, in_1[6]);
endmodule

module is1113 (
  input  [15:0] in_1,
  output out_2
);

  wire and_1_out, and_2_out, not_1_out, not_2_out, not_3_out;

  not not_1 (not_1_out, in_1[8]);
  not not_2 (not_2_out, in_1[6]);
  not not_3 (not_3_out, in_1[8]);
  and and_1 (and_1_out, in_1[9], not_1_out, not_2_out);
  and and_2 (and_2_out, in_1[9], not_3_out, in_1[7]);
  or or_1 (out_2, and_1_out, and_2_out);
endmodule

module is15 (
  input  [15:0] in_1,
  output z
);

  wire not_1_out;

  not not_1 (not_1_out, in_1[7]);
  and and_1 (z, in_1[9], in_1[8], not_1_out, in_1[6]);
endmodule

module IsP1 (
  input  [15:0] in_1,
  output S
);

  wire and_1_out, and_2_out, and_3_out, and_4_out, not_1_out, not_2_out, not_3_out, not_4_out, not_5_out,
       not_6_out;

  not not_1 (not_1_out, in_1[9]);
  not not_2 (not_2_out, in_1[7]);
  not not_3 (not_3_out, in_1[9]);
  not not_4 (not_4_out, in_1[6]);
  and and_1 (and_1_out, not_1_out, in_1[8], not_2_out, in_1[6]);
  and and_2 (and_2_out, not_3_out, in_1[8], in_1[7], not_4_out);
  not not_5 (not_5_out, in_1[8]);
  and and_3 (and_3_out, in_1[9], not_5_out, in_1[6]);
  not not_6 (not_6_out, in_1[8]);
  and and_4 (and_4_out, in_1[9], not_6_out, in_1[7]);
  or or_1 (S, and_1_out, and_2_out, and_3_out, and_4_out);
endmodule

module isP2 (
  input  [15:0] in_1,
  output out_2
);

  wire isp1_1_s, isp3_1_s;

  IsP1 isp1_1 (.in_1(in_1), .S(isp1_1_s));
  isP3 isp3_1 (.in_1(in_1), .S(isp3_1_s));
  nor nor_1 (out_2, isp1_1_s, isp3_1_s);
endmodule

module isP3 (
  input  [15:0] in_1,
  output S
);

  wire not_1_out;

  not not_1 (not_1_out, in_1[7]);
  and and_1 (S, in_1[9], in_1[8], not_1_out, in_1[6]);
endmodule

module Opcode_Decoder (
  input  [5:0] Opcode,
  output Shift,
  output Data_Processing,
  output Load_Store,
  output SP_Address,
  output Conditional
);

  isBranch isbranch_1 (.a(Opcode[5]), .b(Opcode[4]), .c(Opcode[3]), .d(Opcode[2]), .s(Conditional));
  isShiftAddSubMov isshiftaddsubmov_1 (.a(Opcode[5]), .b(Opcode[4]), .s(Shift));
  isDataProcessing isdataprocessing_1 (
    .a(Opcode[5]), .b(Opcode[4]), .c(Opcode[3]), .d(Opcode[2]), .e(Opcode[1]), .f(Opcode[0]),
    .s(Data_Processing));
  isLoadStore isloadstore_1 (.a(Opcode[5]), .b(Opcode[4]), .c(Opcode[3]), .d(Opcode[2]), .s(Load_Store));
  isSP_Adress issp_adress_1 (.a(Opcode[5]), .b(Opcode[4]), .c(Opcode[3]), .d(Opcode[2]), .s(SP_Address));

  // Notes on the sheet:
  //   Shift, add, sub, mov
  //   Load/Store
  //   SP Address
  //   Conditional branch
  //   Data Processing
endmodule

module Shift_Add_Sub_Mov (
  input  [15:0] Instruction,
  input  Enable,
  output [3:0] ALU_Opcode,
  output [3:0] Flags_Update_Mask,
  output Carry,
  output [2:0] Rm,
  output [2:0] Rn,
  output [2:0] Rd,
  output [4:0] Imm5,
  output [31:0] Imm32,
  output Imm32_Enable
);

  wire is5BNotMOV, isAddAddImm, isAddSub, isAddSubImm, isMenus1, isMOVImm, isSubSubImm, multiplexer_9_out,
       or_1_out, or_2_out, or_3_out, or_7_out;
  wire [1:0] bit_extender_4_out, bit_extender_5_out, or_6_out, shifter_1_out;
  wire [2:0] multiplexer_10_out, multiplexer_11_out, multiplexer_12_out;
  wire [3:0] multiplexer_1_out, multiplexer_2_out, multiplexer_4_out, multiplexer_5_out, multiplexer_6_out,
       or_4_out, or_5_out;
  wire [4:0] multiplexer_13_out;
  wire [31:0] bit_extender_1_out, bit_extender_2_out, bit_extender_3_out, multiplexer_3_out,
       multiplexer_14_out, subtractor_1_out;

  // Probe on 16'h26ff
  // Probe on 16'h26ff
  and and_1 (isMenus1, Instruction[7], Instruction[6], Instruction[5], Instruction[4], Instruction[3], Instruction[2], Instruction[1], Instruction[0]);
  // Probe on Instruction[7:0]
  Multiplexer #(.width(4), .enable("false")) multiplexer_1 (
    .in0(4'b0000), .in1(4'b1110), .out(multiplexer_1_out), .sel(is5BNotMOV));
  MOVImm movimm_1 (
    .a(Instruction[15]), .b(Instruction[14]), .c(Instruction[13]), .d(Instruction[12]), .e(Instruction[11]),
    .z(isMOVImm));
  AddSub addsub_1 (
    .a(Instruction[13]), .b(Instruction[12]), .c(Instruction[11]), .d(Instruction[10]), .e(Instruction[9]),
    .z(isAddSub));
  assign bit_extender_1_out = {{24{1'b0}}, Instruction[7:0]};  // Bit_Extender bit_extender_1
  assign bit_extender_2_out = {{24{1'b1}}, Instruction[7:0]};  // Bit_Extender bit_extender_2
  fiveNotMOV fivenotmov_1 (
    .a(Instruction[15]), .b(Instruction[14]), .c(Instruction[13]), .d(Instruction[12]), .e(Instruction[11]),
    .z(is5BNotMOV));
  or or_1 (or_1_out, is5BNotMOV, isMOVImm);
  Multiplexer #(.width(4), .enable("false")) multiplexer_2 (
    .in0(4'b0000), .in1(4'b1100), .out(multiplexer_2_out), .sel(isMOVImm));
  // Probe on multiplexer_3_out
  Multiplexer #(.width(32), .enable("false")) multiplexer_3 (
    .in0(bit_extender_1_out), .in1(bit_extender_2_out), .out(multiplexer_3_out), .sel(isMenus1));
  // Probe on multiplexer_4_out
  Multiplexer #(.select(3), .width(4)) multiplexer_4 (
    .in0(4'b0010), .in1(4'b0011), .in2(4'b0100), .in4(4'b1001), .out(multiplexer_4_out),
    .sel(Instruction[13:11]), .en(or_1_out));  // open: in3, in5, in6, in7
  // Probe on multiplexer_1_out
  // Probe on multiplexer_2_out
  Subtractor #(.width(32)) subtractor_1 (
    .a({32{1'b0}}), .b(multiplexer_3_out), .out(subtractor_1_out));  // open: bin, bout
  // Probe on Instruction[8:6]
  Multiplexer #(.select(2), .width(4)) multiplexer_5 (
    .in0(4'b0101), .in1(4'b0110), .in2(4'b0101), .in3(4'b0110), .out(multiplexer_5_out),
    .sel(Instruction[10:9]), .en(or_2_out));
  // Probe on multiplexer_5_out
  or or_2 (or_2_out, isAddSub, isAddSubImm);
  Multiplexer #(.width(4), .enable("false")) multiplexer_6 (
    .in0(4'b0000), .in1(4'b1111), .out(multiplexer_6_out), .sel(or_3_out));
  or or_3 (or_3_out, isAddSub, isAddSubImm);
  // Probe on subtractor_1_out
  assign bit_extender_3_out = {{29{1'b0}}, Instruction[8:6]};  // Bit_Extender bit_extender_3
  // Probe on bit_extender_3_out
  assign bit_extender_4_out = {{1{1'b0}}, isMOVImm};  // Bit_Extender bit_extender_4
  assign bit_extender_5_out = {{1{1'b0}}, isAddSubImm};  // Bit_Extender bit_extender_5
  assign or_4_out = multiplexer_4_out | multiplexer_5_out;  // OR_Gate or_4, 4 bits wide
  // Probe on multiplexer_6_out
  // Probe on bit_extender_4_out
  Shifter #(.width(2)) shifter_1 (.in(bit_extender_5_out), .\dist (1'b1), .out(shifter_1_out));
  // Probe on shifter_1_out
  AddAddImm addaddimm_1 (
    .a(Instruction[13]), .b(Instruction[12]), .c(Instruction[11]), .d(Instruction[10]), .e(Instruction[9]),
    .z(isAddAddImm));
  SubSubImm subsubimm_1 (
    .a(Instruction[13]), .b(Instruction[12]), .c(Instruction[11]), .d(Instruction[10]), .e(Instruction[9]),
    .z(isSubSubImm));
  AddSubImm addsubimm_1 (
    .a(Instruction[13]), .b(Instruction[12]), .c(Instruction[11]), .d(Instruction[10]), .e(Instruction[9]),
    .z(isAddSubImm));
  // Probe on or_4_out
  assign or_5_out = multiplexer_1_out | multiplexer_2_out | multiplexer_6_out;  // OR_Gate or_5, 4 bits wide
  assign or_6_out = bit_extender_4_out | shifter_1_out;  // OR_Gate or_6, 2 bits wide
  Multiplexer #(.width(4), .enable("false")) multiplexer_7 (
    .in0(4'b0000), .in1(or_4_out), .out(ALU_Opcode), .sel(Enable));
  Multiplexer #(.width(4), .enable("false")) multiplexer_8 (
    .in0(4'b0000), .in1(or_5_out), .out(Flags_Update_Mask), .sel(Enable));
  Multiplexer #(.enable("false")) multiplexer_9 (.in0(1'b0), .in1(1'b1), .out(multiplexer_9_out), .sel(isSubSubImm));
  Multiplexer #(.width(3), .enable("false")) multiplexer_10 (
    .in0(3'b000), .in1(Instruction[8:6]), .out(multiplexer_10_out), .sel(isAddSub));
  Multiplexer #(.width(3), .enable("false")) multiplexer_11 (
    .in0(Instruction[5:3]), .in1(3'b000), .out(multiplexer_11_out), .sel(isMOVImm));
  Multiplexer #(.width(3), .enable("false")) multiplexer_12 (
    .in0(Instruction[2:0]), .in1(Instruction[10:8]), .out(multiplexer_12_out), .sel(isMOVImm));
  Multiplexer #(.width(5), .enable("false")) multiplexer_13 (
    .in0({5{1'b0}}), .in1(Instruction[10:6]), .out(multiplexer_13_out), .sel(is5BNotMOV));
  Multiplexer #(.select(2), .width(32), .enable("false")) multiplexer_14 (
    .in0({32{1'b0}}), .in1(subtractor_1_out), .in2(bit_extender_3_out), .out(multiplexer_14_out),
    .sel(or_6_out));  // open: in3
  or or_7 (or_7_out, or_6_out[1], or_6_out[0]);
  Multiplexer #(.enable("false")) multiplexer_15 (.in0(1'b0), .in1(multiplexer_9_out), .out(Carry), .sel(Enable));
  Multiplexer #(.width(3), .enable("false")) multiplexer_16 (
    .in0(3'b000), .in1(multiplexer_10_out), .out(Rm), .sel(Enable));
  Multiplexer #(.width(3), .enable("false")) multiplexer_17 (
    .in0(3'b000), .in1(multiplexer_11_out), .out(Rn), .sel(Enable));
  Multiplexer #(.width(3), .enable("false")) multiplexer_18 (
    .in0(3'b000), .in1(multiplexer_12_out), .out(Rd), .sel(Enable));
  Multiplexer #(.width(5), .enable("false")) multiplexer_19 (
    .in0({5{1'b0}}), .in1(multiplexer_13_out), .out(Imm5), .sel(Enable));
  Multiplexer #(.width(32), .enable("false")) multiplexer_20 (
    .in0({32{1'b0}}), .in1(multiplexer_14_out), .out(Imm32), .sel(Enable));
  Multiplexer #(.enable("false")) multiplexer_21 (.in0(1'b0), .in1(or_7_out), .out(Imm32_Enable), .sel(Enable));

  // Other names for the same wires on the sheet: eightTo10[2:0] = Instruction[10:8]; sixTo8[2:0] = Instruction[8:6];
  //   sixTo10[4:0] = Instruction[10:6]; nineTo10[1:0] = Instruction[10:9]; nineTo13[4:0] = Instruction[13:9];
  //   isEnable = Enable; elevenTo13[2:0] = Instruction[13:11]; zeroTo2[2:0] = Instruction[2:0];
  //   zeroTo7[7:0] = Instruction[7:0]; threeTo5[2:0] = Instruction[5:3]; sixTo7[1:0] = Instruction[7:6]

  // Notes on the sheet:
  //   Pull output low on Enable = 0
  //   Note: ALU uses Rn register for shifts. Use Rn instead of Rm for shifts (immediate) here too
  //   Note 2: MOV uses RSB ALU opcode with Imm8 reversed so that it is copied to output register
  //   Note 3: Imm32_Enable forces the use of the immediate for Rm register
  //   Enable carry for SUB since it is reversed in ALU
  //   ALU will use Imm32 instead of Rm
endmodule

module Data_Processing (
  input  [15:0] Instruction,
  input  Enable,
  output [2:0] Rn,
  output [2:0] Rd,
  output [2:0] Rm,
  output [3:0] ALU_Opcode,
  output [3:0] Flags_Update_Mask
);

  wire is110, is144, is155, is11133, is15166, isp1_1_s, isp2_1_out_2, isp3_1_s, or_1_out, or_2_out, or_4_out;
  wire [2:0] multiplexer_1_out, multiplexer_2_out, multiplexer_5_out, multiplexer_6_out, RD_t, RM_t, RN_t;
  wire [3:0] flag, multiplexer_4_out, multiplexer_7_out, multiplexer_8_out;

  or or_1 (or_1_out, is110, is144, is15166, is11133);
  Multiplexer #(.width(3), .enable("false")) multiplexer_1 (
    .in0(3'b000), .in1(Instruction[2:0]), .out(multiplexer_1_out), .sel(or_2_out));
  or or_2 (or_2_out, is110, is11133);
  Multiplexer #(.width(3), .enable("false")) multiplexer_2 (
    .in0(3'b000), .in1(Instruction[5:3]), .out(multiplexer_2_out), .sel(is15166));
  Multiplexer #(.width(3), .enable("false")) multiplexer_3 (
    .in0(3'b000), .in1(Instruction[2:0]), .out(RD_t), .sel(or_1_out));
  IsP1 isp1_1 (.in_1(Instruction), .S(isp1_1_s));
  // Probe on Instruction
  Multiplexer #(.width(4), .enable("false")) multiplexer_4 (
    .in0(4'b0000), .in1(4'b1111), .out(multiplexer_4_out), .sel(isp1_1_s));
  assign RN_t = multiplexer_1_out | multiplexer_2_out;  // OR_Gate or_3, 3 bits wide
  or or_4 (or_4_out, is110, is11133, is144);
  Multiplexer #(.width(3), .enable("false")) multiplexer_5 (
    .in0(3'b000), .in1(Instruction[2:0]), .out(multiplexer_5_out), .sel(is155));
  isP2 isp2_1 (.in_1(Instruction), .out_2(isp2_1_out_2));
  Multiplexer #(.width(3), .enable("false")) multiplexer_6 (
    .in0(3'b000), .in1(Instruction[5:3]), .out(multiplexer_6_out), .sel(or_4_out));
  tenFirst tenfirst_1 (.in_1(Instruction), .z(is110));
  is1113 is1113_1 (.in_1(Instruction), .out_2(is11133));
  is14 is14_1 (.in_1(Instruction), .z(is144));
  is1516 is1516_1 (.in_1(Instruction), .z(is15166));
  is15 is15_1 (.in_1(Instruction), .z(is155));
  Multiplexer #(.width(4), .enable("false")) multiplexer_7 (
    .in0(4'b0000), .in1(4'b1110), .out(multiplexer_7_out), .sel(isp2_1_out_2));
  assign RM_t = multiplexer_6_out | multiplexer_5_out;  // OR_Gate or_5, 3 bits wide
  isP3 isp3_1 (.in_1(Instruction), .S(isp3_1_s));
  Multiplexer #(.width(4), .enable("false")) multiplexer_8 (
    .in0(4'b0000), .in1(4'b1100), .out(multiplexer_8_out), .sel(isp3_1_s));
  Multiplexer #(.width(3), .enable("false")) multiplexer_9 (.in0(3'b000), .in1(RN_t), .out(Rn), .sel(Enable));
  Multiplexer #(.width(3), .enable("false")) multiplexer_10 (.in0(3'b000), .in1(RD_t), .out(Rd), .sel(Enable));
  Multiplexer #(.width(3), .enable("false")) multiplexer_11 (.in0(3'b000), .in1(RM_t), .out(Rm), .sel(Enable));
  Multiplexer #(.width(4), .enable("false")) multiplexer_12 (
    .in0(4'b0000), .in1(Instruction[9:6]), .out(ALU_Opcode), .sel(Enable));
  Multiplexer #(.width(4), .enable("false")) multiplexer_13 (
    .in0(4'b0000), .in1(flag), .out(Flags_Update_Mask), .sel(Enable));
  assign flag = multiplexer_4_out | multiplexer_7_out | multiplexer_8_out;  // OR_Gate or_6, 4 bits wide

  // Other names for the same wires on the sheet: instruc[15:0] = Instruction; zeroTo2[2:0] = Instruction[2:0];
  //   opcode[3:0] = Instruction[9:6]; sel = Enable; threeTo5[2:0] = Instruction[5:3]

  // Notes on the sheet:
  //   Pull output low on Enable = 0
endmodule

module Flags_APSR (
  input  [3:0] Flags_In,
  input  [3:0] Update_Mask,
  input  Clk,
  input  Reset,
  output [3:0] Flags_Out
);

  wire and_1_out, and_2_out, and_3_out, and_4_out, and_5_out, and_6_out, and_7_out, and_8_out, not_1_out,
       not_2_out, not_3_out, not_4_out;

  and and_1 (and_1_out, Flags_In[0], Update_Mask[0]);
  not not_1 (not_1_out, Flags_In[0]);
  and and_2 (and_2_out, not_1_out, Update_Mask[0]);
  and and_3 (and_3_out, Flags_In[1], Update_Mask[1]);
  not not_2 (not_2_out, Flags_In[1]);
  and and_4 (and_4_out, not_2_out, Update_Mask[1]);
  and and_5 (and_5_out, Flags_In[2], Update_Mask[2]);
  not not_3 (not_3_out, Flags_In[2]);
  and and_6 (and_6_out, not_3_out, Update_Mask[2]);
  and and_7 (and_7_out, Flags_In[3], Update_Mask[3]);
  not not_4 (not_4_out, Flags_In[3]);
  and and_8 (and_8_out, not_4_out, Update_Mask[3]);
  S_R_Flip_Flop s_r_ff_1 (
    .S(and_1_out), .R(and_2_out), .clk(Clk), .Q(Flags_Out[0]), .reset(Reset));  // open: Qn, preset
  S_R_Flip_Flop s_r_ff_2 (
    .S(and_3_out), .R(and_4_out), .clk(Clk), .Q(Flags_Out[1]), .reset(Reset));  // open: Qn, preset
  S_R_Flip_Flop s_r_ff_3 (
    .S(and_5_out), .R(and_6_out), .clk(Clk), .Q(Flags_Out[2]), .reset(Reset));  // open: Qn, preset
  S_R_Flip_Flop s_r_ff_4 (
    .S(and_7_out), .R(and_8_out), .clk(Clk), .Q(Flags_Out[3]), .reset(Reset));  // open: Qn, preset
endmodule

module Load_Store (
  input  [15:0] Instruction,
  input  Enable,
  input  [31:0] Stack_Pointer,
  input  Clk,
  input  Reset,
  output Store,
  output Load,
  output PC_Hold,
  output [2:0] Rm,
  output [2:0] Rd,
  output [31:0] RAM_Addr,
  output init2
);

  wire and_1_out, and_2_out, d_ff_1_q, d_ff_2_qn, d_ff_3_q, d_ff_4_q, d_ff_5_q, d_ff_5_qn, init,
       multiplexer_3_out, multiplexer_4_out, not_1_out, not_2_out, not_3_out, undriven;
  wire [31:0] adder_1_out, bit_extender_1_out;

  Clock clktest ();  // open: out
  // Probe on Instruction[7:0]
  D_Flip_Flop d_ff_1 (.D(1'b1), .clk(Clk), .Q(d_ff_1_q));  // open: Qn, preset, reset
  assign bit_extender_1_out = {{24{1'b0}}, Instruction[7:0]};  // Bit_Extender bit_extender_1
  // Probe on d_ff_1_q
  Multiplexer #(.enable("false")) multiplexer_1 (.in0(1'b1), .in1(1'b0), .out(init2), .sel(d_ff_1_q));
  Adder #(.width(32)) adder_1 (.a(bit_extender_1_out), .b(Stack_Pointer), .out(adder_1_out));  // open: cin, cout
  // Probe on adder_1_out
  not not_1 (not_1_out, Instruction[11]);
  D_Flip_Flop d_ff_2 (.D(d_ff_2_qn), .Qn(d_ff_2_qn));  // open: clk, Q, preset, reset
  D_Flip_Flop d_ff_3 (.D(not_3_out), .clk(Clk), .Q(d_ff_3_q), .reset(Reset));  // open: Qn, preset
  D_Flip_Flop d_ff_4 (.D(not_2_out), .clk(Clk), .Q(d_ff_4_q), .reset(Reset));  // open: Qn, preset
  D_Flip_Flop d_ff_5 (.D(d_ff_5_qn), .Q(d_ff_5_q), .Qn(d_ff_5_qn), .preset(init), .reset(undriven));  // open: clk
  Multiplexer #(.enable("false")) multiplexer_2 (.in0(1'b0), .in1(not_1_out), .out(Store), .sel(Enable));
  not not_2 (not_2_out, multiplexer_3_out);
  Multiplexer #(.enable("false")) multiplexer_3 (.in0(d_ff_4_q), .in1(1'b1), .out(multiplexer_3_out), .sel(init2));
  not not_3 (not_3_out, multiplexer_4_out);
  Multiplexer #(.enable("false")) multiplexer_4 (.in0(d_ff_3_q), .in1(1'b0), .out(multiplexer_4_out), .sel(init2));
  Multiplexer #(.enable("false")) multiplexer_5 (.in0(1'b0), .in1(multiplexer_3_out), .out(PC_Hold), .sel(and_2_out));
  Multiplexer #(.width(3), .enable("false")) multiplexer_6 (
    .in0(3'b000), .in1(Instruction[10:8]), .out(Rm), .sel(Enable));
  Multiplexer #(.width(3), .enable("false")) multiplexer_7 (
    .in0(3'b000), .in1(Instruction[10:8]), .out(Rd), .sel(Enable));
  Multiplexer #(.width(32), .enable("false")) multiplexer_8 (
    .in0({32{1'b0}}), .in1(adder_1_out), .out(RAM_Addr), .sel(Enable));
  and and_1 (and_1_out, Enable, Instruction[11]);
  and and_2 (and_2_out, Instruction[11], Enable);
  Multiplexer #(.enable("false")) multiplexer_9 (.in0(1'b0), .in1(multiplexer_4_out), .out(Load), .sel(and_1_out));

  // Other names for the same wires on the sheet: tun_isLDR = Instruction[11]; isFirstREdge = init2;
  //   tun_imm8[7:0] = Instruction[7:0]; tun_Rt[2:0] = Instruction[10:8]; tunEnable = Enable

  // Notes on the sheet:
  //   Delay load and hold PC for 1 cycle for the RAM to send out requested data 
endmodule

module SP_Address (
  input  Enable,
  input  [15:0] Instruction,
  input  [31:0] Stack_Pointer,
  output Write_Enable,
  output [31:0] New_Stack_Pointer
);

  wire [31:0] adder_1_out, bit_extender_1_out, multiplexer_1_out, subtractor_1_out;

  assign bit_extender_1_out = {{25{1'b0}}, Instruction[6:0]};  // Bit_Extender bit_extender_1
  // Probe on nothing
  Subtractor #(.width(32)) subtractor_1 (
    .a(bit_extender_1_out), .b(Stack_Pointer), .out(subtractor_1_out));  // open: bin, bout
  Adder #(.width(32)) adder_1 (.a(bit_extender_1_out), .b(Stack_Pointer), .out(adder_1_out));  // open: cin, cout
  Multiplexer #(.width(32), .enable("false")) multiplexer_1 (
    .in0(adder_1_out), .in1(subtractor_1_out), .out(multiplexer_1_out), .sel(Instruction[7]));
  Multiplexer #(.width(32), .enable("false")) multiplexer_2 (
    .in0({32{1'b0}}), .in1(multiplexer_1_out), .out(New_Stack_Pointer), .sel(Enable));

  assign Write_Enable = Enable;

  // Other names for the same wires on the sheet: imm7[6:0] = Instruction[6:0]; isEnableSPA = Enable;
  //   sp[31:0] = Stack_Pointer

  // Notes on the sheet:
  //   Pull output low on Enable = 0
endmodule

module fiveNotMOV (
  input  a,
  input  b,
  input  c,
  input  d,
  input  e,
  output z
);

  wire and_1_out, and_2_out, not_1_out, not_2_out, not_3_out, not_4_out, not_5_out, not_6_out, not_7_out,
       not_8_out;

  not not_1 (not_1_out, a);
  not not_2 (not_2_out, b);
  not not_3 (not_3_out, c);
  not not_4 (not_4_out, d);
  not not_5 (not_5_out, a);
  not not_6 (not_6_out, b);
  not not_7 (not_7_out, c);
  not not_8 (not_8_out, e);
  and and_1 (and_1_out, not_1_out, not_2_out, not_3_out, not_4_out);
  and and_2 (and_2_out, not_5_out, not_6_out, not_7_out, not_8_out);
  or or_1 (z, and_1_out, and_2_out);
endmodule

module MOVImm (
  input  a,
  input  b,
  input  c,
  input  d,
  input  e,
  output z
);

  wire not_1_out, not_2_out, not_3_out, not_4_out;

  not not_1 (not_1_out, a);
  not not_2 (not_2_out, b);
  not not_3 (not_3_out, d);
  not not_4 (not_4_out, e);
  and and_1 (z, not_1_out, not_2_out, c, not_3_out, not_4_out);
endmodule

module AddSub (
  input  a,
  input  b,
  input  c,
  input  d,
  input  e,
  output z
);

  wire and_1_out, and_2_out, not_1_out, not_2_out, not_3_out, not_4_out, not_5_out;

  not not_1 (not_1_out, a);
  not not_2 (not_2_out, d);
  not not_3 (not_3_out, e);
  not not_4 (not_4_out, a);
  not not_5 (not_5_out, d);
  and and_1 (and_1_out, not_1_out, b, c, not_2_out, not_3_out);
  and and_2 (and_2_out, not_4_out, b, c, not_5_out, e);
  or or_1 (z, and_1_out, and_2_out);
endmodule

module AddSubImm (
  input  a,
  input  b,
  input  c,
  input  d,
  input  e,
  output z
);

  wire and_1_out, and_2_out, not_1_out, not_2_out, not_3_out;

  not not_1 (not_1_out, a);
  not not_2 (not_2_out, e);
  not not_3 (not_3_out, a);
  and and_1 (and_1_out, not_1_out, b, c, d, not_2_out);
  and and_2 (and_2_out, not_3_out, b, c, d, e);
  or or_1 (z, and_1_out, and_2_out);
endmodule

module brouillon (
  input  Reset,
  input  Clk,
  input  [3:0] Flags_In,
  input  [3:0] Update_Mask,
  output [3:0] Flags_Out
);

  wire addsub_1_p6, and_1_out, is5BNotMOV, isMOVImm, not_1_out, not_2_out;
  wire [1:0] bit_extender_1_out, bit_extender_2_out, or_1_out, shifter_1_out;
  wire [2:0] sixTo8, threeTo5;
  wire [4:0] nineTo13;

  // AddSub addsub_1: pin names not known; wires that end beside it: nineTo13[4], nineTo13[3], nineTo13[2], nineTo13[1], nineTo13[0], addsub_1_p6
  // Probe on addsub_1_p6
  not not_1 (not_1_out, isMOVImm);
  not not_2 (not_2_out, is5BNotMOV);
  assign bit_extender_1_out = {{1{1'b0}}, is5BNotMOV};  // Bit_Extender bit_extender_1
  // Probe on bit_extender_1_out
  and and_1 (and_1_out, addsub_1_p6, not_1_out, not_2_out);
  Shifter #(.width(2)) shifter_1 (.in(bit_extender_1_out), .\dist (1'b1), .out(shifter_1_out));
  assign bit_extender_2_out = {{1{1'b0}}, and_1_out};  // Bit_Extender bit_extender_2
  // Probe on bit_extender_2_out
  // Probe on shifter_1_out
  Load_Store load_store_1 (.Instruction({16{1'b0}}));  // open: Rm, Rd, Load, Enable, RAM_Addr, Stack_Pointer, Store, PC_Hold, Reset, Clk, init2
  Multiplexer #(.select(2), .width(3), .enable("false")) multiplexer_1 (
    .in0(3'b000), .in1(sixTo8), .in2(threeTo5), .sel(or_1_out));  // open: in3, out
  assign or_1_out = bit_extender_2_out | shifter_1_out;  // OR_Gate or_1, 2 bits wide
  S_R_Flip_Flop s_r_ff_1 (
    .S(Flags_In[0]), .R(Update_Mask[0]), .clk(Clk), .Q(Flags_Out[0]), .reset(Reset));  // open: Qn, preset
  S_R_Flip_Flop s_r_ff_2 (
    .S(Flags_In[1]), .R(Update_Mask[1]), .clk(Clk), .Q(Flags_Out[1]), .reset(Reset));  // open: Qn, preset
  S_R_Flip_Flop s_r_ff_3 (
    .S(Update_Mask[2]), .R(Flags_In[2]), .clk(Clk), .Q(Flags_Out[2]), .reset(Reset));  // open: Qn, preset
  S_R_Flip_Flop s_r_ff_4 (
    .S(Update_Mask[3]), .R(Flags_In[3]), .clk(Clk), .Q(Flags_Out[3]), .reset(Reset));  // open: Qn, preset
endmodule

module AddAddImm (
  input  a,
  input  b,
  input  c,
  input  d,
  input  e,
  output z
);

  wire and_1_out, and_2_out, not_1_out, not_2_out, not_3_out, not_4_out, not_5_out;

  not not_1 (not_1_out, a);
  not not_2 (not_2_out, d);
  not not_3 (not_3_out, e);
  not not_4 (not_4_out, a);
  not not_5 (not_5_out, e);
  and and_1 (and_1_out, not_1_out, b, c, not_2_out, not_3_out);
  and and_2 (and_2_out, not_4_out, b, c, d, not_5_out);
  or or_1 (z, and_1_out, and_2_out);
endmodule

module SubSubImm (
  input  a,
  input  b,
  input  c,
  input  d,
  input  e,
  output z
);

  wire and_1_out, and_2_out, not_1_out, not_2_out, not_3_out;

  not not_1 (not_1_out, a);
  not not_2 (not_2_out, d);
  not not_3 (not_3_out, a);
  and and_1 (and_1_out, not_1_out, b, c, not_2_out, e);
  and and_2 (and_2_out, not_3_out, b, c, d, e);
  or or_1 (z, and_1_out, and_2_out);
endmodule

module testDecoder (
);

  wire opcode_decoder_1_conditional, opcode_decoder_1_data_processing, opcode_decoder_1_load_store,
       opcode_decoder_1_shift, opcode_decoder_1_sp_address;

  // Probe on 6'b100110
  Opcode_Decoder opcode_decoder_1 (
    .Opcode(6'b100110), .Shift(opcode_decoder_1_shift), .Data_Processing(opcode_decoder_1_data_processing),
    .Load_Store(opcode_decoder_1_load_store), .SP_Address(opcode_decoder_1_sp_address),
    .Conditional(opcode_decoder_1_conditional));
endmodule

module isDataProcessing (
  input  a,
  input  b,
  input  c,
  input  d,
  input  e,
  input  f,
  output s
);

  wire not_1_out, not_2_out, not_3_out, not_4_out, not_5_out;

  not not_1 (not_1_out, a);
  not not_2 (not_2_out, c);
  not not_3 (not_3_out, d);
  not not_4 (not_4_out, e);
  not not_5 (not_5_out, f);
  and and_1 (s, not_1_out, b, not_2_out, not_3_out, not_4_out, not_5_out);
endmodule

module isShiftAddSubMov (
  input  a,
  input  b,
  output s
);

  wire not_1_out, not_2_out;

  not not_1 (not_1_out, a);
  not not_2 (not_2_out, b);
  and and_1 (s, not_1_out, not_2_out);
endmodule

module isLoadStore (
  input  a,
  input  b,
  input  c,
  input  d,
  output s
);

  wire not_1_out, not_2_out;

  not not_1 (not_1_out, b);
  not not_2 (not_2_out, c);
  and and_1 (s, a, not_1_out, not_2_out, d);
endmodule

module isSP_Adress (
  input  a,
  input  b,
  input  c,
  input  d,
  output s
);

  wire not_1_out;

  not not_1 (not_1_out, b);
  and and_1 (s, a, not_1_out, c, d);
endmodule

module isBranch (
  input  a,
  input  b,
  input  c,
  input  d,
  output s
);

  wire not_1_out;

  not not_1 (not_1_out, c);
  and and_1 (s, a, b, not_1_out, d);
endmodule

module brouillon_Load_Store (
);

  wire d_ff_1_q, not_1_out, not_2_out, not_3_out, not_4_out, not_5_out, not_6_out, not_7_out, not_8_out,
       undriven, undriven_2, xnor_1_out, xnor_2_out, xnor_3_out, xnor_4_out, xor_1_out;

  xor xor_1 (xor_1_out, undriven, not_3_out);
  not not_1 (not_1_out, not_4_out);
  not not_2 (not_2_out, not_1_out);
  not not_3 (not_3_out, not_2_out);
  not not_4 (not_4_out, not_5_out);
  not not_5 (not_5_out, not_7_out);
  D_Flip_Flop d_ff_1 (.D(undriven), .clk(xor_1_out), .Q(d_ff_1_q));  // open: Qn, preset, reset
  not not_6 (not_6_out, d_ff_1_q);
  not not_7 (not_7_out, not_8_out);
  not not_8 (not_8_out, not_6_out);
  xnor xnor_1 (xnor_1_out, undriven_2, undriven_2);
  xnor xnor_2 (xnor_2_out, xnor_1_out, xnor_1_out);
  xnor xnor_3 (xnor_3_out, xnor_2_out, xnor_2_out);
  xnor xnor_4 (xnor_4_out, xnor_3_out, undriven_2);
endmodule
