// Logisim project Machine.circ as structural Verilog: 3 circuits, main circuit main
module main (
  input  GPIO_A1,
  input  GPIO_A3,
  input  GPIO_A5,
  input  GPIO_A7,
  input  GPIO_A9,
  input  GPIO_A11,
  input  GPIO_A13,
  input  GPIO_A15,
  input  GPIO_A17,
  input  GPIO_A19,
  input  GPIO_A21,
  input  GPIO_A23,
  input  GPIO_A25,
  input  GPIO_A27,
  input  GPIO_A29,
  input  GPIO_A31,
  input  GPIO_A33,
  input  GPIO_A35,
  input  GPIO_B1,
  input  GPIO_B3,
  input  GPIO_B5,
  input  GPIO_B7,
  input  GPIO_B9,
  input  GPIO_B11,
  input  GPIO_B13,
  input  GPIO_B15,
  input  GPIO_B17,
  input  GPIO_B19,
  input  GPIO_B21,
  input  GPIO_B23,
  input  GPIO_B25,
  input  GPIO_B27,
  input  GPIO_B29,
  input  GPIO_B31,
  input  GPIO_B33,
  input  GPIO_B35,
  output GPIO_A2,
  output GPIO_A4,
  output GPIO_A6,
  output GPIO_A8,
  output GPIO_A10,
  output GPIO_A12,
  output GPIO_A14,
  output GPIO_A16,
  output GPIO_A18,
  output GPIO_A20,
  output GPIO_A22,
  output GPIO_A24,
  output GPIO_A26,
  output GPIO_A28,
  output GPIO_A30,
  output GPIO_A32,
  output GPIO_A34,
  output GPIO_A36,
  output GPIO_B2,
  output GPIO_B4,
  output GPIO_B6,
  output GPIO_B8,
  output GPIO_B10,
  output GPIO_B12,
  output GPIO_B14,
  output GPIO_B16,
  output GPIO_B18,
  output GPIO_B20,
  output GPIO_B22,
  output GPIO_B24,
  output GPIO_B26,
  output GPIO_B28,
  output GPIO_B30,
  output GPIO_B32,
  output GPIO_B34,
  output GPIO_B36
);

  wire Clk_Button_out, clk_out, CPU_1_store, Rst_Button_out;
  wire [7:0] RAM_Addr, ROM_Addr;
  wire [15:0] ROMa_data;
  wire [31:0] CPU_1_r0, CPU_1_r1, CPU_1_r2, CPU_1_r3, CPU_1_r4, CPU_1_r5, CPU_1_r6, CPU_1_r7, CPU_1_ram_out,
       RAMa_dout;
  wire [31:8] CPU_1_ram_addr;

  RAM #(.dataWidth(32), .databus("bibus")) RAMa (
    .addr(RAM_Addr), .we(CPU_1_store), .oe(1'b1), .clk(clk_out), .din(CPU_1_ram_out), .dout(RAMa_dout));
  Clock sysclk ();  // open: out
  Clock clk (.out(clk_out));
  LED A0 (.in(RAMa_dout[0]));
  LED A1 (.in(RAMa_dout[1]));
  LED A2 (.in(RAMa_dout[2]));
  ROM #(.dataWidth(16)) ROMa (.addr(ROM_Addr), .data(ROMa_data));
  Button Clk_Button (.out(Clk_Button_out));
  Button Rst_Button (.out(Rst_Button_out));
  LED A3 (.in(RAMa_dout[3]));
  LED A4 (.in(RAMa_dout[4]));
  LED A5 (.in(RAMa_dout[5]));
  LED A6 (.in(RAMa_dout[6]));
  LED A7 (.in(RAMa_dout[7]));
  LED L0 (.in(CPU_1_r0[0]));
  // Probe on CPU_1_r1
  // Probe on CPU_1_r0
  LED L3 (.in(CPU_1_r0[3]));
  LED L1 (.in(CPU_1_r0[1]));
  LED L2 (.in(CPU_1_r0[2]));
  // Probe on CPU_1_r3
  // Probe on CPU_1_r2
  // Probe on CPU_1_r5
  // Probe on CPU_1_r4
  // Probe on ROMa_data
  LED L4 (.in(CPU_1_r0[4]));
  LED L5 (.in(CPU_1_r0[5]));
  // Probe on CPU_1_r7
  // Probe on CPU_1_r6
  CPU CPU_1 (
    .ROM_Addr(ROM_Addr), .RAM_In(RAMa_dout), .R3(CPU_1_r3), .R7(CPU_1_r7), .R2(CPU_1_r2), .R6(CPU_1_r6),
    .RAM_Addr({CPU_1_ram_addr, RAM_Addr}), .R1(CPU_1_r1), .R5(CPU_1_r5), .ROM_In(ROMa_data), .R0(CPU_1_r0),
    .R4(CPU_1_r4), .Clk(clk_out), .RAM_Out(CPU_1_ram_out), .Reset(Rst_Button_out), .Store(CPU_1_store));
  // Probe on CPU_1_store
  LED L6 (.in(CPU_1_r0[6]));
  LED L7 (.in(CPU_1_r0[7]));
  // Probe on ROM_Addr
  LED LED_1 (.in(RAM_Addr[0]));
  LED LED_2 (.in(RAM_Addr[1]));
  LED LED_3 (.in(RAM_Addr[2]));
  // Probe on CPU_1_ram_out
  // Probe on RAM_Addr
  LED LED_4 (.in(RAM_Addr[3]));
  LED LED_5 (.in(RAM_Addr[4]));
  LED LED_6 (.in(RAM_Addr[5]));
  LED LED_7 (.in(RAM_Addr[6]));
  LED LED_8 (.in(RAM_Addr[7]));

  // Notes on the sheet:
  //   contents of ROMa (hex, n*v repeats v):
  //   b0a0 2302 930c 2304 9310 2301 9304 2300 9308 de11 9b04 9a0c 4353 9304 9b08 1c5b 9308 9a08 9b10 429a
  //   db0a 2301 9314 9a14 9b10 9318 921c 9b1c 9a18 4093 9314 9a04 9b14 429a d125 2300 de26 23ff 931c 981c
  //   b020
  //   Use only 8 bit adresses
  //   VCC 5V
  //   VCC 3.3V
  //   VCC 5V
  //   VCC 3.3V
  //   GROUND
  //   GROUND
  //   GROUND
  //   GROUND
endmodule

module CPU (
  input  [31:0] RAM_In,
  input  [15:0] ROM_In,
  input  Clk,
  input  Reset,
  output [7:0] ROM_Addr,
  output [31:0] R3,
  output [31:0] R7,
  output [31:0] R2,
  output [31:0] R6,
  output [31:0] RAM_Addr,
  output [31:0] R1,
  output [31:0] R5,
  output [31:0] R0,
  output [31:0] R4,
  output [31:0] RAM_Out,
  output Store
);

  wire Controller_1_carry, imm_32_enable, load_0e5808d6, tun_dp_shift;
  wire [2:0] Controller_1_rd, Controller_1_rm, Controller_1_rn;
  wire [3:0] ALU_1_flags, Controller_1_alu_opcode;
  wire [4:0] alu_shift, cpu_5_faible_1_s, imm_5;
  wire [31:0] a_alu, A_out, ALU_out, B_out, data_in, imm_32;

  // Probe on A_out
  // Probe on Controller_1_rd
  Controller Controller_1 (
    .Imm5(imm_5), .Imm32(imm_32), .Rn(Controller_1_rn), .Inst(ROM_In), .ALU_Opcode(Controller_1_alu_opcode),
    .Rd(Controller_1_rd), .Flags(ALU_1_flags), .Rm(Controller_1_rm), .PC(ROM_Addr),
    .Imm32_Enable(imm_32_enable), .DP_Shift(tun_dp_shift), .Carry(Controller_1_carry), .RAM_Addr(RAM_Addr),
    .Load(load_0e5808d6), .Store(Store), .Clk(Clk), .Reset(Reset));
  CPU_5_faible cpu_5_faible_1 (.a(A_out), .s(cpu_5_faible_1_s));
  Multiplexer #(.width(32), .enable("false")) multiplexer_1 (
    .in0(A_out), .in1(imm_32), .out(a_alu), .sel(imm_32_enable));
  // Probe on data_in
  Multiplexer #(.width(5), .enable("false")) multiplexer_2 (
    .in0(cpu_5_faible_1_s), .in1(imm_5), .out(alu_shift), .sel(tun_dp_shift));
  // Probe on Controller_1_rm
  // Probe on Controller_1_alu_opcode
  // Probe on a_alu
  BancRegistre bancregistre_1 (
    .Clk(Clk), .Reset(Reset), .DataIn(data_in), .RegB(Controller_1_rn), .RegA(Controller_1_rm),
    .RegDest(Controller_1_rd), .AOut(A_out), .BOut(B_out), .R0(R0), .R1(R1), .R2(R2), .R3(R3), .R4(R4),
    .R5(R5), .R6(R6), .R7(R7));
  // Probe on Controller_1_rn
  // Probe on B_out
  // Probe on alu_shift
  ALU ALU_1 (
    .A(a_alu), .B(B_out), .Codop(Controller_1_alu_opcode), .CarryIn(Controller_1_carry), .Shift(alu_shift),
    .S(ALU_out), .Flags(ALU_1_flags));
  // Probe on ALU_1_flags
  // Probe on ALU_out
  Multiplexer #(.width(32), .enable("false")) multiplexer_3 (.in0({32{1'b0}}), .in1(A_out), .out(RAM_Out), .sel(Store));
  Multiplexer #(.width(32), .enable("false")) multiplexer_4 (
    .in0(ALU_out), .in1(RAM_In), .out(data_in), .sel(load_0e5808d6));

  // Other names for the same wires on the sheet: ramram_in[31:0] = RAM_In; store_3a0089b5 = Store
endmodule

module CPU_5_faible (
  input  [31:0] a,
  output [4:0] s
);


  assign s = a[4:0];
endmodule
